// Logisim project Aquecedor_SD_V1.0.circ as structural Verilog: 4 circuits, main circuit main
module main (
  input  BL,
  input  BM,
  input  BO,
  output MV,
  output R1,
  output R2,
  output SE,
  output MO,
  output SD
);

  wire clock_1_out, n2_tick_clock_1_sd, n2_tick_clock_1_se;

  Clock clock_1 (.out(clock_1_out));
  _2_tick_clock u_2_tick_clock_1 (
    .BL(BL), .BO(BO), .SE(n2_tick_clock_1_se), .SD(n2_tick_clock_1_sd), .CLK(clock_1_out));
  Modulo_de_funcionamento modulo_de_funcionamento_1 (.V(MV), .R1(R1), .R2(R2), .BL(BL), .BM(BM), .CLK(clock_1_out));
  \Modulo_de_oscilação  \modulo_de_oscilação_1  (
    .BL(BL), .BO(BO), .SE(n2_tick_clock_1_se), .SD(n2_tick_clock_1_sd), .MO(MO), .SE_2(SE), .SD_2(SD));
endmodule

module Modulo_de_funcionamento (
  input  BL,
  input  BM,
  input  CLK,
  output V,
  output R1,
  output R2
);

  wire and_1_out, and_2_out, and_3_out, and_4_out, and_5_out, not_1_out, or_1_out, or_2_out, X0_q, X1_q,
       X1_qn;

  not not_1 (not_1_out, BL);
  and and_1 (and_1_out, X1_q, BM);
  and and_2 (and_2_out, X1_q, not_1_out);
  and and_3 (and_3_out, BM, BL, X0_q);
  and and_4 (and_4_out, X1_qn, BM, BL);
  and and_5 (and_5_out, X0_q, not_1_out);
  T_Flip_Flop X1 (.clk(CLK), .T(or_1_out), .Q(X1_q), .Qn(X1_qn));  // open: preset, reset, en
  or or_1 (or_1_out, and_1_out, and_2_out, and_3_out);
  T_Flip_Flop X0 (.clk(CLK), .T(or_2_out), .Q(X0_q));  // open: Qn, preset, reset, en
  or or_2 (or_2_out, and_4_out, and_5_out);
  and and_6 (R1, BL, X1_qn);
  and and_7 (R2, BL, X0_q);

  assign V = BL;
endmodule

module \Modulo_de_oscilação  (
  input  BL,
  input  BO,
  input  SE,
  input  SD,
  output SE_2,
  output SD_2,
  output MO
);

  wire and_1_out, and_2_out, and_3_out, and_4_out, and_5_out, and_6_out, clock_1_out, not_1_out, not_2_out,
       not_3_out, not_4_out, or_1_out, X_q, X_qn;

  not not_1 (not_1_out, BL);
  not not_2 (not_2_out, SD);
  not not_3 (not_3_out, SE);
  not not_4 (not_4_out, BO);
  and and_1 (and_1_out, not_3_out, not_2_out);
  and and_2 (and_2_out, SE, SD);
  and and_3 (and_3_out, BL, BO, not_3_out, SD, X_qn);
  and and_4 (and_4_out, BL, BO, SE, not_2_out, X_qn);
  Clock clock_1 (.out(clock_1_out));
  or or_1 (or_1_out, not_1_out, not_4_out, and_1_out, and_2_out, and_3_out, and_4_out);
  T_Flip_Flop X (.clk(clock_1_out), .T(or_1_out), .Q(X_q), .Qn(X_qn));  // open: preset, reset, en
  and and_5 (and_5_out, X_q, SD, not_3_out, BO, BL);
  or or_2 (MO, and_5_out, and_6_out);
  and and_6 (and_6_out, X_q, not_2_out, SE, BO, BL);

  assign SD_2 = SD;
  assign SE_2 = SE;
endmodule

module _2_tick_clock (
  input  BL,
  input  BO,
  input  CLK,
  output SE,
  output SD
);

  wire and_1_out, and_2_out, X0_q;

  and and_1 (and_1_out, BL, BO, X0_q);
  and and_2 (and_2_out, BO, BL);
  T_Flip_Flop X1 (.clk(CLK), .T(and_1_out), .Q(SE), .Qn(SD));  // open: preset, reset, en
  T_Flip_Flop X0 (.clk(CLK), .T(and_2_out), .Q(X0_q));  // open: Qn, preset, reset, en
endmodule
